# Fritzing sketch buttonLED (saved by Fritzing 1.0.0rc)
breadboards: 1

parts:
  7_Segment_LED = 7 Segment Display
  R1 = Resistor [tolerance=±5% power=0.25W resistance=220 package=THT]
  R2 = Resistor [tolerance=±5% power=0.25W resistance=220 package=THT]
  R3 = Resistor [tolerance=±5% power=0.25W resistance=220 package=THT]
  R4 = Resistor [tolerance=±5% power=0.25W resistance=220 package=THT]
  R5 = Resistor [tolerance=±5% power=0.25W resistance=220 package=THT]
  R6 = Resistor [tolerance=±5% power=0.25W resistance=220 package=THT]
  R7 = Resistor [tolerance=±5% power=0.25W resistance=220 package=THT]
  R8 = Resistor [tolerance=±5% power=0.25W resistance=220 package=THT]
  Incement = Pushbutton [package="[THT]"]
  Random = Pushbutton [package="[THT]"]
  Arduino = Arduino Uno (Rev3)

nets:
  N1: 7_Segment_LED.Segment_E, R3.Pin_1
  N2: 7_Segment_LED.Segment_D, R4.Pin_1
  N3: 7_Segment_LED.common_cathode, Incement.Pin_3, Incement.Pin_4, Random.Pin_3, Random.Pin_4, Arduino.GND
  N4: 7_Segment_LED.Segment_C, R2.Pin_0
  N5: 7_Segment_LED.Segment_DP, R1.Pin_0
  N6: 7_Segment_LED.Segment_B, R6.Pin_0
  N7: 7_Segment_LED.Segment_A, R5.Pin_0
  N8: 7_Segment_LED.Segment_F, R7.Pin_1
  N9: 7_Segment_LED.Segment_G, R8.Pin_1
  N10: R1.Pin_1, Arduino.D13/SCK
  N11: R2.Pin_1, Arduino.D4
  N12: R3.Pin_0, Arduino.D6_PWM
  N13: R4.Pin_0, Arduino.D5_PWM
  N14: R5.Pin_1, Arduino.D2
  N15: R6.Pin_1, Arduino.D3_PWM
  N16: R7.Pin_0, Arduino.D7
  N17: R8.Pin_0, Arduino.D8
  N18: Incement.Pin_1, Incement.Pin_2, Arduino.A0
  N19: Random.Pin_1, Random.Pin_2, Arduino.A1
