# Fritzing sketch buttonLED (saved by Fritzing 1.0.0rc)
breadboards: 1

parts:
  7_Segment_LED = 7 Segment Display
  R5 = Resistor [tolerance=±5% power=0.25W resistance=100 package=THT]
  R7 = Resistor [tolerance=±5% power=0.25W resistance=100 package=THT]
  Increment = Pushbutton [package="[THT]"]
  Random = Pushbutton [package="[THT]"]
  Arduino = Arduino Uno (Rev3)
  R9 = Resistor [tolerance=±5% power=0.25W resistance=100 package=THT]
  R10 = Resistor [tolerance=±5% power=0.25W resistance=100 package=THT]
  R11 = Resistor [tolerance=±5% power=0.25W resistance=100 package=THT]
  R12 = Resistor [tolerance=±5% power=0.25W resistance=100 package=THT]
  R13 = Resistor [tolerance=±5% power=0.25W resistance=100 package=THT]
  R14 = Resistor [tolerance=±5% power=0.25W resistance=100 package=THT]

nets:
  N1: 7_Segment_LED.Segment_E, R11.Pin_1
  N2: 7_Segment_LED.Segment_D, R12.Pin_1
  N3: 7_Segment_LED.common_cathode, Increment.Pin_3, Increment.Pin_4, Random.Pin_3, Random.Pin_4, Arduino.GND
  N4: 7_Segment_LED.Segment_C, R14.Pin_0
  N5: 7_Segment_LED.Segment_DP, R13.Pin_0
  N6: 7_Segment_LED.Segment_B, R10.Pin_0
  N7: 7_Segment_LED.Segment_A, R5.Pin_0
  N8: 7_Segment_LED.Segment_F, R7.Pin_1
  N9: 7_Segment_LED.Segment_G, R9.Pin_1
  N10: R5.Pin_1, Arduino.D2
  N11: R7.Pin_0, Arduino.D7
  N12: Increment.Pin_1, Increment.Pin_2, Arduino.A0
  N13: Random.Pin_1, Random.Pin_2, Arduino.A1
  N14: Arduino.D8, R9.Pin_0
  N15: Arduino.D13/SCK, R13.Pin_1
  N16: Arduino.D3_PWM, R10.Pin_1
  N17: Arduino.D4, R14.Pin_1
  N18: Arduino.D5_PWM, R12.Pin_0
  N19: Arduino.D6_PWM, R11.Pin_0
